# Fritzing sketch Kabel API (saved by Fritzing 0.9.3b)
breadboards: 1

parts:
  Bauteil1 = Arduino Mega 2560 (Rev3)
  Bauteil2 = Arduino GSM Shield
  U1 = LCD-16X2 [package=lcd-16x2_noholes]
  LED1 = smd LED [color="Red (633nm)" package="0603 [SMD]"]
  LED2 = smd LED [color="Green (565nm)" package="0603 [SMD]"]
  R2 = Resistor [tolerance=±5% resistance=330 package=THT]
  R3 = Resistor [tolerance=±5% resistance=330 package=THT]
  U2 = POT [package=alps_pot]
  DHT1 = DHT22 Humidity and Temperature Sensor
  R4 = Resistor [tolerance=±5% resistance=330 package=THT]
  ZS-042_RTC1 = ZS-042 RTC Module
  Bauteil3 = Adafruit_BMP280
  Bauteil4 = Adafruit CCS811
  Bauteil5 = MQ-9 breakout

nets:
  N1: Bauteil1.A0, Bauteil5.AO
  N2: Bauteil1.A4, R4.Pin_0
  N3: Bauteil1.D21/SCL, ZS-042_RTC1.SCL, Bauteil4.SCL
  N4: Bauteil1.D20/SDA, ZS-042_RTC1.SDA, Bauteil4.SDA
  GND: Bauteil1.GND, Bauteil2.AGND, U1.VSS, U1.R_W, U1.K, LED1.cathode, LED2.cathode, U2.A, DHT1.NULL, DHT1.GND, ZS-042_RTC1.GND, Bauteil3.GND, Bauteil4.GND, Bauteil4.!WAKE, Bauteil5.GND
  N5: Bauteil1.D13_PWM, U1.RS
  N6: Bauteil1.D12_PWM, U1.E
  N7: Bauteil1.D11_PWM, Bauteil2.DSM_RX_D2
  N8: Bauteil1.D10_PWM, Bauteil2.DSM_TX_D3
  N9: Bauteil1.D9_PWM, Bauteil2.RST_MDM/D7
  N10: Bauteil1.D8_PWM, R2.Pin_1
  3V3: Bauteil1.3V3, U2.E, DHT1.VDD, Bauteil4.VIN
  5V: Bauteil1.5V, Bauteil2.5V, U1.VDD, ZS-042_RTC1.VCC, Bauteil3.VIN, Bauteil5.VCC
  N11: Bauteil1.D2_PWM, U1.DB7
  N12: Bauteil1.D3_PWM, U1.DB6
  N13: Bauteil1.D4_PWM, U1.DB5
  N14: Bauteil1.D5_PWM, U1.DB4
  N15: Bauteil1.D6_PWM, DHT1.DATA
  N16: Bauteil1.D7_PWM, R3.Pin_1
  N17: Bauteil1.D28, Bauteil3.SCK/SCL
  N18: Bauteil1.D30, Bauteil3.SDO/ADR
  N19: Bauteil1.D32, Bauteil3.SDI/SDA
  N20: Bauteil1.D34, Bauteil3.CS
  N21: U1.VO, U2.S
  N22: U1.A, R4.Pin_1
  N23: LED1.anode, R2.Pin_0
  N24: LED2.anode, R3.Pin_0

custom parts:
  Adafruit_BMP280: Bosch has stepped up their game with their new BMP280 sensor, an environmental sensor with temperature, barometric pressure that is the next generation upgrade to the BMP085/BMP180/BMP183. This sensor is great for all sorts of weather sensing and can even be used in both I2C and SPI! This precision sensor from Bosch is the best low-cost, precision sensing solution for measuring barometric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
  MQ-9 breakout: SKU: 101284
